// Logisim project ruc36_lab6.circ as structural Verilog: 1 circuit, main circuit main
module main (
);

  wire _7, _7_t, and_1_out, button_1_out, CLK, clock_1_out, count__7, decoder_1_out0, decoder_1_out1,
       decoder_1_out2, decoder_1_out3, decoder_1_out4, decoder_1_out5, decoder_1_out6, decoder_1_out7,
       decoder_1_out8, decoder_1_out9, decoder_1_out10, decoder_1_out11, decoder_1_out12, decoder_1_out13,
       decoder_1_out14, decoder_1_out15, Lose, Lose1, not_1_p2, or_2_out, STOP, win;
  wire [3:0] adder_1_out, count;

  Clock clock_1 (.out(clock_1_out));
  Button button_1 (.out(button_1_out));
  or or_1 (CLK, clock_1_out, button_1_out);
  Adder #(.width(4)) adder_1 (.a(count), .b(4'b0001), .out(adder_1_out));  // open: cin, cout
  Register #(.width(4)) register_1 (.D(adder_1_out), .en(not_1_p2), .Q(count), .clk(CLK));  // open: clr
  LED led_1 (.in(decoder_1_out0));
  and and_1 (and_1_out, STOP, 1'b1);
  LED led_2 (.in(decoder_1_out2));
  LED led_3 (.in(decoder_1_out4));
  LED led_4 (.in(decoder_1_out3));
  LED led_5 (.in(decoder_1_out1));
  Decoder #(.select(4)) decoder_1 (
    .out0(decoder_1_out0), .out1(decoder_1_out1), .out2(decoder_1_out2), .out3(decoder_1_out3),
    .out4(decoder_1_out4), .out5(decoder_1_out5), .out6(decoder_1_out6), .out7(decoder_1_out7),
    .out8(decoder_1_out8), .out9(decoder_1_out9), .out10(decoder_1_out10), .out11(decoder_1_out11),
    .out12(decoder_1_out12), .out13(decoder_1_out13), .out14(decoder_1_out14), .out15(decoder_1_out15),
    .sel(count));  // open: en
  // NOT_Gate not_1: pin names not known; wires that end beside it: and_1_out, not_1_p2
  and and_2 (Lose1, STOP, _7_t);
  and and_3 (Lose, STOP, _7);
  and and_4 (win, count__7, STOP);
  Button button_2 (.out(STOP));
  LED led_6 (.in(decoder_1_out5));
  LED led_7 (.in(decoder_1_out7));
  LED led_8 (.in(decoder_1_out8));
  LED u__7 (.in(decoder_1_out6));
  LED led_9 (.in(win));
  LED led_10 (.in(decoder_1_out9));
  LED led_11 (.in(decoder_1_out12));
  LED led_12 (.in(decoder_1_out11));
  LED led_13 (.in(decoder_1_out10));
  LED led_14 (.in(or_2_out));
  or or_2 (or_2_out, Lose1, Lose);
  LED led_15 (.in(decoder_1_out14));
  LED led_16 (.in(decoder_1_out15));
  LED led_17 (.in(decoder_1_out13));
  Comparator #(.width(4)) comparator_1 (.a(count), .b(4'b0111), .gt(_7_t), .eq(count__7), .lt(_7));

  // Notes on the sheet:
  //   v
  //   Win!
  //   Lose
endmodule
