// Logisim project ruc36_lab7.circ as structural Verilog: 1 circuit, main circuit main
module main (
);

  wire _3, button_1_out, CLK, clock_1_out;
  wire [1:0] Inst;
  wire [3:0] ACC, ACC_1, ACC_1_t, adder_1_out, buffer_1_out, DISP_q, MUXOUTPUT, Q;

  Clock clock_1 (.out(clock_1_out));
  Button button_1 (.out(button_1_out));
  or or_1 (CLK, clock_1_out, button_1_out);
  Register #(.width(4)) register_1 (.D(adder_1_out), .Q(Q), .clk(CLK));  // open: en, clr
  Adder #(.width(4)) adder_1 (.a(Q), .b(4'b0001), .out(adder_1_out));  // open: cin, cout
  assign buffer_1_out = ACC;  // Buffer buffer_1, 4 bits wide
  Register #(.width(4)) DISP (.D(ACC), .en(_3), .Q(DISP_q), .clk(CLK));  // open: clr
  // Probe on Inst
  Multiplexer #(.select(2), .width(4)) multiplexer_1 (
    .in0(4'b0000), .in1(ACC_1), .in2(ACC_1_t), .in3(buffer_1_out), .out(MUXOUTPUT), .sel(Inst));  // open: en
  Hex_Digit_Display hex_digit_display_1 (.value(DISP_q));  // open: dp
  Comparator #(.width(2)) comparator_1 (.a(Inst), .b(2'b11), .eq(_3));  // open: gt, lt
  Adder #(.width(4)) adder_2 (.a(ACC), .b(4'b0001), .out(ACC_1));  // open: cin, cout
  Subtractor #(.width(4)) subtractor_1 (.a(ACC), .b(4'b0001), .out(ACC_1_t));  // open: bin, bout
  Register #(.width(4)) u_ACC (.D(MUXOUTPUT), .Q(ACC), .clk(CLK));  // open: en, clr
  ROM #(.addrWidth(4), .dataWidth(2)) rom_1 (.addr(Q), .data(Inst));  // open: sel

  // Notes on the sheet:
  //   instructions
  //   0: ACC = 0
  //   1: ACC = ACC + 1
  //   2: ACC = ACC - 1
  //   3: DISP = ACC, ACC = ACC
  //   contents of rom_1 (hex, n*v repeats v):
  //   0 5*1 3 2 2 3 4*1 3 2
endmodule
