// Logisim project ruc36_lab8.circ as structural Verilog: 3 circuits, main circuit main
module main (
  input  [7:0] ALU_A,
  input  [7:0] ALU_B,
  input  [2:0] ALU_Op,
  input  [7:0] REG_rd,
  input  [2:0] rd,
  input  Reg_WE,
  input  [2:0] rs,
  input  [2:0] rt
);

  wire CLK, clock_1_out, tick_out;
  wire [7:0] ALU_Out, REG_rs, REG_rt;

  Clock clock_1 (.out(clock_1_out));
  or or_1 (CLK, clock_1_out, tick_out);
  Button tick (.out(tick_out));
  // Probe on ALU_A
  // Probe on ALU_B
  // Probe on ALU_Out
  // Probe on REG_rd
  // Probe on REG_rs
  // Probe on REG_rt
  ALU alu_1 (.A(ALU_A), .B(ALU_B), .ALU_Op(ALU_Op), .ALU_Out(ALU_Out));
  // Probe on ALU_Op
  // Probe on ALU_Out
  Register_File register_file_1 (
    .CLK(CLK), .rs(rs), .rt(rt), .rd(rd), .Reg_WE(Reg_WE), .Reg__rd(REG_rd), .REG_rs(REG_rs), .REG_rt(REG_rt));
endmodule

module ALU (
  input  [7:0] A,
  input  [7:0] B,
  input  [2:0] ALU_Op,
  output [7:0] ALU_Out
);

  wire [2:0] B_2_0;
  wire [7:0] adder_1_out, and_1_out, not_1_out, or_1_p3, shifter_1_out, shifter_2_out, subtractor_1_out,
       xor_1_out;

  Bit_Extender #(.out_width(3)) bit_extender_1 (.in(B), .out(B_2_0));
  Adder adder_1 (.a(A), .b(B), .out(adder_1_out));  // open: cin, cout
  Subtractor subtractor_1 (.a(A), .b(B), .out(subtractor_1_out));  // open: bin, bout
  assign and_1_out = A & B;  // AND_Gate and_1, 8 bits wide
  // OR_Gate #(.width(8)) or_1: pin names not known; wires that end beside it: A, B, or_1_p3
  assign xor_1_out = A ^ B;  // XOR_Gate xor_1, 8 bits wide
  // NOT_Gate not_1 has open pins: in=open, out=not_1_out
  Shifter shifter_1 (.in(A), .\dist (B_2_0), .out(shifter_1_out));
  Shifter #(.shift("lr")) shifter_2 (.in(A), .\dist (B_2_0), .out(shifter_2_out));
  Multiplexer #(.select(3), .width(8)) multiplexer_1 (
    .in0(adder_1_out), .in1(subtractor_1_out), .in2(and_1_out), .in3(or_1_p3), .in4(xor_1_out),
    .in5(not_1_out), .in6(shifter_1_out), .in7(shifter_2_out), .out(ALU_Out), .sel(ALU_Op));  // open: en

  // Other names for the same wires on the sheet: rd[2:0] = ALU_Op
endmodule

module Register_File (
  input  CLK,
  input  [2:0] rs,
  input  [2:0] rt,
  input  [2:0] rd,
  input  Reg_WE,
  input  [7:0] Reg__rd,
  output [7:0] REG_rs,
  output [7:0] REG_rt
);

  wire decoder_1_out0, decoder_1_out1, decoder_1_out2, decoder_1_out3, decoder_1_out4, decoder_1_out5,
       decoder_1_out6, decoder_1_out7;
  wire [7:0] register_1_q, register_2_q, register_3_q, register_4_q, register_5_q, register_6_q,
       register_7_q, register_8_q;

  Decoder #(.select(3), .disabled(0), .enable("true")) decoder_1 (
    .out0(decoder_1_out0), .out1(decoder_1_out1), .out2(decoder_1_out2), .out3(decoder_1_out3),
    .out4(decoder_1_out4), .out5(decoder_1_out5), .out6(decoder_1_out6), .out7(decoder_1_out7), .sel(rd),
    .en(Reg_WE));
  Register register_1 (.D(Reg__rd), .en(decoder_1_out0), .Q(register_1_q), .clk(CLK));  // open: clr
  Register register_2 (.D(Reg__rd), .en(decoder_1_out1), .Q(register_2_q), .clk(CLK));  // open: clr
  Register register_3 (.D(Reg__rd), .en(decoder_1_out2), .Q(register_3_q), .clk(CLK));  // open: clr
  Register register_4 (.D(Reg__rd), .en(decoder_1_out3), .Q(register_4_q), .clk(CLK));  // open: clr
  Register register_5 (.D(Reg__rd), .en(decoder_1_out4), .Q(register_5_q), .clk(CLK));  // open: clr
  Register register_6 (.D(Reg__rd), .en(decoder_1_out5), .Q(register_6_q), .clk(CLK));  // open: clr
  Register register_7 (.D(Reg__rd), .en(decoder_1_out6), .Q(register_7_q), .clk(CLK));  // open: clr
  Register register_8 (.D({8{1'b0}}), .en(decoder_1_out7), .Q(register_8_q), .clk(CLK));  // open: clr
  Multiplexer #(.select(3), .width(8), .disabled(0)) multiplexer_1 (
    .in0(register_1_q), .in1(register_2_q), .in2(register_3_q), .in3(register_4_q), .in4(register_5_q),
    .in5(register_6_q), .in6(register_7_q), .in7(register_8_q), .out(REG_rs), .sel(rs));  // open: en
  Multiplexer #(.select(3), .width(8), .disabled(0)) multiplexer_2 (
    .in0(register_1_q), .in1(register_2_q), .in2(register_3_q), .in3(register_4_q), .in4(register_5_q),
    .in5(register_6_q), .in6(register_7_q), .in7(register_8_q), .out(REG_rt), .sel(rt));  // open: en
endmodule
