// Logisim project ruc36_project2.circ as structural Verilog: 7 circuits, main circuit main
module main (
);

  wire Branch, button_1_out, CLK, clock_1_out, Control_alu_imm, Control_imm_signed, Display, halt, Jump, ld,
       lui, Mov, RegWe, st;
  wire [2:0] Control_aluop, Control_rd, Control_rs, Control_rt;
  wire [3:0] Display_digits_1, Display_digits_2, Display_digits_3, Display_digits_4;
  wire [4:0] Control_opcode;
  wire [7:0] Imm, PC_pc;
  wire [15:0] A, ALU_alu_out, bit_extender_1_out, bit_extender_2_out, bit_extender_3_out, bit_extender_4_out,
       data_to_load, multiplexer_1_out, multiplexer_2_out, multiplexer_3_out, multiplexer_4_out,
       multiplexer_5_out, PC_1, Register_reg_rt, RS;
  wire [21:0] rom_1_data;

  Clock clock_1 (.out(clock_1_out));
  or or_1 (CLK, clock_1_out, button_1_out);
  Button button_1 (.out(button_1_out));
  Hex_Digit_Display hex_digit_display_1 (.value(Display_digits_4));  // open: dp
  // Probe on RS
  assign bit_extender_1_out = {{8{Imm[7]}}, Imm};  // Bit_Extender bit_extender_1
  PC PC (
    .offset(bit_extender_1_out), .Branch(Branch), .target(RS), .Jump(Jump), .CLK(CLK), .Halt(halt),
    .PC(PC_pc), .PC_1(PC_1));
  Hex_Digit_Display hex_digit_display_2 (.value(Display_digits_3));  // open: dp
  Hex_Digit_Display hex_digit_display_3 (.value(Display_digits_2));  // open: dp
  display u_Display (
    .Data(RS), .WE(Display), .CLK(CLK), .Digits_1(Display_digits_1), .Digits_2(Display_digits_2),
    .Digits_3(Display_digits_3), .Digits_4(Display_digits_4));  // open: Clear
  // Probe on PC_pc
  LED u_Halt (.in(halt));
  Hex_Digit_Display hex_digit_display_4 (.value(Display_digits_1));  // open: dp
  assign bit_extender_2_out = {{8{Imm[7]}}, Imm};  // Bit_Extender bit_extender_2
  assign bit_extender_3_out = {{8{1'b0}}, Imm};  // Bit_Extender bit_extender_3
  Multiplexer #(.width(16)) multiplexer_1 (
    .in0(ALU_alu_out), .in1(data_to_load), .out(multiplexer_1_out), .sel(ld));  // open: en
  RAM #(.addrWidth(16), .dataWidth(16), .bus("separate")) ram_1 (
    .addr(ALU_alu_out), .din(Register_reg_rt), .data(data_to_load), .str(st), .clk(CLK), .ld(ld));  // open: sel, clr
  Multiplexer #(.width(16), .disabled(0)) multiplexer_2 (
    .in0(bit_extender_2_out), .in1(bit_extender_3_out), .out(multiplexer_2_out), .sel(Control_imm_signed));  // open: en
  // Probe on multiplexer_2_out
  ROM #(.dataWidth(22)) rom_1 (.addr(PC_pc), .data(rom_1_data));  // open: sel
  // Probe on multiplexer_1_out
  // Probe on Control_rt
  // Probe on Control_rd
  // Probe on Control_rs
  ALU ALU (.ALU_Op(Control_aluop), .A(A), .B(multiplexer_5_out), .ALU_Out(ALU_alu_out));
  // Probe on multiplexer_5_out
  Multiplexer #(.width(16), .disabled(0)) multiplexer_3 (
    .in0(Register_reg_rt), .in1(multiplexer_2_out), .out(multiplexer_3_out), .sel(Control_alu_imm));  // open: en
  Multiplexer #(.width(16), .disabled(0)) multiplexer_4 (
    .in0(multiplexer_3_out), .in1({16{1'b0}}), .out(multiplexer_4_out), .sel(Mov));  // open: en
  Multiplexer #(.width(16), .disabled(0)) multiplexer_5 (
    .in0(multiplexer_4_out), .in1(16'h8), .out(multiplexer_5_out), .sel(lui));  // open: en
  assign bit_extender_4_out = {{8{1'b0}}, Imm};  // Bit_Extender bit_extender_4
  Control Control (
    .Instruction(rom_1_data), .rd(Control_rd), .IMM(Imm), .rt(Control_rt), .rs(Control_rs),
    .Opcode(Control_opcode), .Alu_Imm(Control_alu_imm), .RegWE(RegWe), .ALUOp(Control_aluop),
    .DispWe(Display), .Halt(halt), .Load(ld), .Store(st), .JUMP(Jump), .Lui(lui), .Mov(Mov),
    .Imm_signed(Control_imm_signed));  // open: out_2, RegDataSrc, out_12
  // Probe on RS
  Register Register (
    .CLK(CLK), .rs(Control_rs), .rt(Control_rt), .rd(Control_rd), .Reg_WE(RegWe),
    .DATA_input(multiplexer_1_out), .REG_rs(RS), .REG_rt(Register_reg_rt));
  // Probe on Register_reg_rt
  // Probe on ALU_alu_out
  // Probe on A
  Multiplexer #(.width(16), .disabled(0)) multiplexer_6 (
    .in0(RS), .in1(bit_extender_4_out), .out(A), .sel(lui));  // open: en
  // Probe on Control_aluop
  Branch_Control u_Branch (.ALUOP(ALU_alu_out), .Opcode(Control_opcode), .Branch(Branch));

  // Notes on the sheet:
  //   contents of rom_1 (hex, n*v repeats v):
  //   41040 41280 404c0 c0219 dfe1a 406c0 a0118 402c0 a0158 20020 20028
endmodule

module display (
  input  [15:0] Data,
  input  WE,
  input  Clear,
  input  CLK,
  output [3:0] Digits_1,
  output [3:0] Digits_2,
  output [3:0] Digits_3,
  output [3:0] Digits_4
);

  wire or_1_out;
  wire [15:0] multiplexer_1_out;

  Multiplexer #(.width(16)) multiplexer_1 (
    .in0(Data), .in1({16{1'b0}}), .out(multiplexer_1_out), .sel(Clear));  // open: en
  or or_1 (or_1_out, WE, Clear);
  Register_part #(.width(16)) register_1 (
    .D(multiplexer_1_out), .en(or_1_out), .Q({Digits_4, Digits_3, Digits_2, Digits_1}), .clk(CLK));  // open: clr
endmodule

module PC (
  input  [15:0] offset,
  input  Branch,
  input  [15:0] target,
  input  Jump,
  input  CLK,
  input  Halt,
  output [7:0] PC,
  output [15:0] PC_1
);

  wire not_1_out;
  wire [7:0] adder_1_out, adder_2_out, multiplexer_1_out, multiplexer_2_out, offset_8, target_8;

  Multiplexer #(.width(8)) multiplexer_1 (
    .in0(8'h1), .in1(offset_8), .out(multiplexer_1_out), .sel(Branch));  // open: en
  Adder adder_1 (.a(PC), .b(multiplexer_1_out), .out(adder_1_out));  // open: cin, cout
  Bit_Extender #(.in_width(16), .out_width(8), .\type ("sign")) bit_extender_1 (.in(offset), .out(offset_8));
  Bit_Extender #(.in_width(16), .out_width(8), .\type ("sign")) bit_extender_2 (.in(target), .out(target_8));
  Multiplexer #(.width(8)) multiplexer_2 (
    .in0(adder_1_out), .in1(target_8), .out(multiplexer_2_out), .sel(Jump));  // open: en
  // Probe on multiplexer_2_out
  Register_part PC_Register (.D(multiplexer_2_out), .en(not_1_out), .Q(PC), .clk(CLK));  // open: clr
  not not_1 (not_1_out, Halt);
  Adder adder_2 (.a(PC), .b(8'h1), .out(adder_2_out));  // open: cin, cout
  assign PC_1 = {{8{adder_2_out[7]}}, adder_2_out};  // Bit_Extender bit_extender_3
endmodule

module ALU (
  input  [2:0] ALU_Op,
  input  [15:0] A,
  input  [15:0] B,
  output [15:0] ALU_Out
);

  wire [3:0] B_3_0;
  wire [15:0] adder_1_out, and_1_out, not_1_out, or_1_p3, shifter_1_out, shifter_2_out, subtractor_1_out,
       xor_1_out;

  Bit_Extender #(.in_width(16), .out_width(4)) bit_extender_1 (.in(B), .out(B_3_0));
  Adder #(.width(16)) adder_1 (.a(A), .b(B), .out(adder_1_out));  // open: cin, cout
  Subtractor #(.width(16)) subtractor_1 (.a(A), .b(B), .out(subtractor_1_out));  // open: bin, bout
  assign and_1_out = A & B;  // AND_Gate and_1, 16 bits wide
  // OR_Gate #(.width(16)) or_1: pin names not known; wires that end beside it: A, B, or_1_p3
  assign xor_1_out = A ^ B;  // XOR_Gate xor_1, 16 bits wide
  // NOT_Gate not_1 has open pins: in=open, out=not_1_out
  Shifter #(.width(16)) shifter_1 (.in(A), .\dist (B_3_0), .out(shifter_1_out));
  Shifter #(.width(16), .shift("lr")) shifter_2 (.in(A), .\dist (B_3_0), .out(shifter_2_out));
  Multiplexer #(.select(3), .width(16)) multiplexer_1 (
    .in0(adder_1_out), .in1(subtractor_1_out), .in2(and_1_out), .in3(or_1_p3), .in4(xor_1_out),
    .in5(not_1_out), .in6(shifter_1_out), .in7(shifter_2_out), .out(ALU_Out), .sel(ALU_Op));  // open: en

  // Other names for the same wires on the sheet: rd[2:0] = ALU_Op
endmodule

module Register (
  input  CLK,
  input  [2:0] rs,
  input  [2:0] rt,
  input  [2:0] rd,
  input  Reg_WE,
  input  [15:0] DATA_input,
  output [15:0] REG_rs,
  output [15:0] REG_rt
);

  wire decoder_1_out0, decoder_1_out1, decoder_1_out2, decoder_1_out3, decoder_1_out4, decoder_1_out5,
       decoder_1_out6, decoder_1_out7;
  wire [15:0] R0_q, R1_q, R2_q, R3_q, R4_q, R5_q, R6_q, R7_q;

  Decoder #(.select(3), .disabled(0), .enable("true")) decoder_1 (
    .out0(decoder_1_out0), .out1(decoder_1_out1), .out2(decoder_1_out2), .out3(decoder_1_out3),
    .out4(decoder_1_out4), .out5(decoder_1_out5), .out6(decoder_1_out6), .out7(decoder_1_out7), .sel(rd),
    .en(Reg_WE));
  Register_part #(.width(16)) R0 (.D({16{1'b0}}), .en(decoder_1_out0), .Q(R0_q), .clk(CLK));  // open: clr
  Register_part #(.width(16)) R1 (.D(DATA_input), .en(decoder_1_out1), .Q(R1_q), .clk(CLK));  // open: clr
  Register_part #(.width(16)) R2 (.D(DATA_input), .en(decoder_1_out2), .Q(R2_q), .clk(CLK));  // open: clr
  Register_part #(.width(16)) R3 (.D(DATA_input), .en(decoder_1_out3), .Q(R3_q), .clk(CLK));  // open: clr
  Register_part #(.width(16)) R4 (.D(DATA_input), .en(decoder_1_out4), .Q(R4_q), .clk(CLK));  // open: clr
  Register_part #(.width(16)) R5 (.D(DATA_input), .en(decoder_1_out5), .Q(R5_q), .clk(CLK));  // open: clr
  Register_part #(.width(16)) R6 (.D(DATA_input), .en(decoder_1_out6), .Q(R6_q), .clk(CLK));  // open: clr
  Register_part #(.width(16)) R7 (.D(DATA_input), .en(decoder_1_out7), .Q(R7_q), .clk(CLK));  // open: clr
  Multiplexer #(.select(3), .width(16), .disabled(0)) multiplexer_1 (
    .in0(R0_q), .in1(R1_q), .in2(R2_q), .in3(R3_q), .in4(R4_q), .in5(R5_q), .in6(R6_q), .in7(R7_q),
    .out(REG_rs), .sel(rs));  // open: en
  Multiplexer #(.select(3), .width(16), .disabled(0)) multiplexer_2 (
    .in0(R0_q), .in1(R1_q), .in2(R2_q), .in3(R3_q), .in4(R4_q), .in5(R5_q), .in6(R6_q), .in7(R7_q),
    .out(REG_rt), .sel(rt));  // open: en

  // Other names for the same wires on the sheet: DATA[15:0] = DATA_input
endmodule

module Control (
  input  [21:0] Instruction,
  output [2:0] out_2,
  output Alu_Imm,
  output [2:0] rd,
  output [2:0] rt,
  output [2:0] rs,
  output [4:0] Opcode,
  output [7:0] IMM,
  output RegDataSrc,
  output RegWE,
  output [2:0] ALUOp,
  output [4:0] out_12,
  output DispWe,
  output Halt,
  output Load,
  output Store,
  output JUMP,
  output Lui,
  output Mov,
  output Imm_signed
);

  wire add, adi, \and , and_1_out, ani, beq, bge, blt, bne, comparator_1_gt, comparator_2_lt, jal_rd__imm,
       jr_rs, li, \not , \or , or_3_out, or_4_out, or_6_out, ori, sbi, shl, shr, sli, sri, sub, \xor , xri;
  wire [2:0] ALUOp_t, multiplexer_1_out, multiplexer_2_out;

  // Probe on Instruction[16:9]
  Decoder #(.select(5), .disabled(0)) decoder_1 (
    .out0(Halt), .out1(DispWe), .out2(li), .out3(Lui), .out4(Mov), .out5(Load), .out6(Store), .out7(add),
    .out8(sub), .out9(\and ), .out10(\or ), .out11(\xor ), .out12(\not ), .out13(shl), .out14(shr),
    .out15(adi), .out16(sbi), .out17(ani), .out18(ori), .out19(xri), .out20(sli), .out21(sri), .out22(JUMP),
    .out23(blt), .out24(bge), .out25(beq), .out26(bne), .out27(jal_rd__imm), .out28(jr_rs),
    .sel(Instruction[21:17]));  // open: out29, out30, out31, en
  or or_1 (RegWE, Lui, Load, add, \and , \xor , shl, adi, ani, xri, sri, li, Mov, sub, \or , \not , shr, sbi, ori, sli, jal_rd__imm);
  Comparator #(.width(5)) comparator_1 (.a(out_12), .b(5'b01111), .gt(comparator_1_gt));  // open: eq, lt
  Comparator #(.width(5)) comparator_2 (.a(out_12), .b(5'b11000), .lt(comparator_2_lt));  // open: gt, eq
  Subtractor #(.width(3)) subtractor_1 (.a(out_12[2:0]), .b(3'b111), .out(ALUOp_t));  // open: bin, bout
  or or_2 (Imm_signed, Store, Load, adi, sbi);
  or or_3 (or_3_out, blt, beq, bge, bne);
  and and_1 (and_1_out, comparator_1_gt, comparator_2_lt);
  or or_4 (or_4_out, li, Lui, Load, Store);
  Priority_Encoder #(.select(5)) priority_encoder_1 (
    .in0(Halt), .in1(DispWe), .in2(li), .in3(Lui), .in4(Mov), .in5(Load), .in6(Store), .in7(add), .in8(sub),
    .in9(\and ), .in10(\or ), .in11(\xor ), .in12(\not ), .in13(shl), .in14(shr), .in15(adi), .in16(sbi),
    .in17(ani), .in18(ori), .in19(xri), .in20(sli), .in21(sri), .in22(JUMP), .in23(blt), .in24(bge),
    .in25(beq), .in26(bne), .in27(jal_rd__imm), .in28(jr_rs), .out(out_12));  // open: in29, in30, in31, gs, en_out, en_in
  Multiplexer #(.width(3)) multiplexer_1 (
    .in0(ALUOp_t), .in1(3'b001), .out(multiplexer_1_out), .sel(or_3_out));  // open: en
  or or_5 (Alu_Imm, and_1_out, or_4_out);
  Multiplexer #(.width(3)) multiplexer_2 (
    .in0(multiplexer_1_out), .in1(3'b000), .out(multiplexer_2_out), .sel(or_6_out));  // open: en
  or or_6 (or_6_out, Load, Store);
  Multiplexer #(.width(3)) multiplexer_3 (.in0(multiplexer_2_out), .in1(3'b110), .out(ALUOp), .sel(Lui));  // open: en

  assign IMM = Instruction[16:9];
  assign Opcode = Instruction[21:17];
  assign out_2 = ALUOp;
  assign rd = Instruction[8:6];
  assign RegDataSrc = Load;
  assign rs = Instruction[5:3];
  assign rt = Instruction[2:0];

  // Other names for the same wires on the sheet: hlt = Halt; _0 = Instruction[0]; _1 = Instruction[1];
  //   _2 = Instruction[2]; _3 = Instruction[3]; _4 = Instruction[4]; _5 = Instruction[5]; _6 = Instruction[6];
  //   _7 = Instruction[7]; _8 = Instruction[8]; _9 = Instruction[9]; _10 = Instruction[10]; _11 = Instruction[11];
  //   _12 = Instruction[12]; _13 = Instruction[13]; _14 = Instruction[14]; _15 = Instruction[15];
  //   _16 = Instruction[16]; j_imm = JUMP; ld = Load; _17 = Instruction[17]; _18 = Instruction[18];
  //   _19 = Instruction[19]; _20 = Instruction[20]; _21 = Instruction[21]; st = Store

  // Notes on the sheet:
  //   DECODING
endmodule

module Branch_Control (
  input  [15:0] ALUOP,
  input  [4:0] Opcode,
  output Branch
);

  wire and_1_out, and_2_p4, and_3_out, comparator_1_eq, comparator_2_eq, comparator_3_eq, comparator_4_eq,
       comparator_4_gt, comparator_4_lt, not_1_p2, or_1_out;

  Comparator #(.width(5)) comparator_1 (.a(Opcode), .b(5'b10111), .eq(comparator_1_eq));  // open: gt, lt
  Comparator #(.width(5)) comparator_2 (.a(Opcode), .b(5'b11000), .eq(comparator_2_eq));  // open: gt, lt
  Comparator #(.width(5)) comparator_3 (.a(Opcode), .b(5'b11001), .eq(comparator_3_eq));  // open: gt, lt
  Comparator #(.width(16)) comparator_4 (
    .a(ALUOP), .b({16{1'b0}}), .gt(comparator_4_gt), .eq(comparator_4_eq), .lt(comparator_4_lt));
  // NOT_Gate not_1: pin names not known; wires that end beside it: comparator_4_eq, not_1_p2
  and and_1 (and_1_out, comparator_4_lt, comparator_1_eq);
  or or_1 (or_1_out, comparator_4_gt, comparator_4_eq);
  // AND_Gate and_2: pin names not known; wires that end beside it: or_1_out, or_1_out, comparator_2_eq, and_2_p4
  and and_3 (and_3_out, not_1_p2, not_1_p2, comparator_3_eq);
  or or_2 (Branch, and_1_out, and_2_p4, and_3_out);
endmodule
